# Fritzing sketch Temporizador con alarma - Fritzing File (saved by Fritzing 0.9.2b)
breadboards: 1

parts:
  Parte1 = Arduino Uno (Rev3)
  R1 = Rotary Potentiometer (Small) [maximum_resistance=100kΩ package=THT]
  LCD1 = LCD screen
  J1 = Piezo Speaker

nets:
  N1: Parte1.D8, LCD1.RS
  N2: Parte1.D9_PWM, LCD1.DB4
  N3: Parte1.D10_PWM/SS, LCD1.DB5
  N4: Parte1.D11_PWM/MOSI, LCD1.DB6
  N5: Parte1.D12/MISO, LCD1.DB7
  N6: Parte1.D4, J1.pin2
  N7: Parte1.D7, LCD1.E
  5V: Parte1.5V, R1.leg1, LCD1.VDD, LCD1.LED+
  GND: Parte1.GND, R1.leg2, LCD1.VSS, LCD1.R/W, LCD1.LED-, J1.pin1
  N8: R1.wiper, LCD1.V0
